// Logisim project Reservior.circ as structural Verilog: 1 circuit, main circuit main
module main (
  input  in_1,
  input  in_2,
  output out_3,
  output out_4,
  output out_5,
  output out_6,
  output out_7
);

  wire and_1_out, and_2_out, and_3_out, and_4_out, and_5_out, and_6_out, and_7_out, and_8_out, and_11_out,
       counter_1_p1, counter_1_p2, counter_2_p1, counter_2_p2, j_k_ff_1_qn, j_k_ff_3_qn, j_k_ff_4_qn,
       j_k_ff_5_q, not_1_out, not_2_out, or_1_out, or_2_out, or_3_out, or_4_out, or_5_out, or_6_out,
       undriven, undriven_2, undriven_3, undriven_4, xor_1_out, xor_2_out, xor_3_out, xor_4_out;

  and and_1 (and_1_out, not_1_out, j_k_ff_3_qn, j_k_ff_3_qn, j_k_ff_1_qn, j_k_ff_1_qn);
  and and_2 (and_2_out, j_k_ff_3_qn, j_k_ff_3_qn, j_k_ff_1_qn);
  not not_1 (not_1_out, in_1);
  Clock clock_1 ();  // open: out
  not not_2 (not_2_out, not_1_out);
  buf and_3 (and_3_out, not_2_out);  // AND_Gate
  // AND_Gate and_4 has open pins: out=and_4_out
  buf and_5 (and_5_out, j_k_ff_3_qn);  // AND_Gate
  buf or_1 (or_1_out, not_2_out);  // OR_Gate
  and and_6 (and_6_out, not_1_out, undriven_2);
  and and_7 (and_7_out, and_6_out, undriven_3);
  buf and_8 (and_8_out, undriven);  // AND_Gate
  xor xor_1 (xor_1_out, undriven_2, or_1_out);
  or or_2 (or_2_out, and_6_out, and_3_out);
  buf or_3 (or_3_out, and_4_out);  // OR_Gate
  // OR_Gate or_4 has open pins: out=or_4_out
  J_K_Flip_Flop j_k_ff_1 (
    .J(undriven_4), .clk(xor_1_out), .Q(out_7), .Qn(j_k_ff_1_qn), .preset(counter_1_p1), .en(counter_1_p2),
    .reset(or_5_out));  // open: K
  // Counter counter_1: pin names not known; wires that end beside it: counter_1_p1, counter_1_p2, and_1_out
  xor xor_2 (xor_2_out, undriven_3, or_2_out);
  buf xor_3 (xor_3_out, undriven);  // XOR_Gate
  // Counter counter_2: pin names not known; wires that end beside it: counter_2_p1, counter_2_p2
  buf xor_4 (xor_4_out, j_k_ff_3_qn);  // XOR_Gate
  J_K_Flip_Flop j_k_ff_2 (
    .J(undriven_4), .K(xor_2_out), .Q(out_6), .Qn(j_k_ff_1_qn), .preset(and_1_out), .en(and_1_out),
    .reset(and_1_out));  // open: clk
  J_K_Flip_Flop j_k_ff_3 (
    .J(undriven_4), .K(xor_3_out), .Q(out_5), .Qn(j_k_ff_3_qn), .preset(counter_2_p1), .en(counter_2_p2),
    .reset(or_5_out));  // open: clk
  J_K_Flip_Flop j_k_ff_4 (
    .J(undriven_4), .K(xor_4_out), .Q(out_4), .Qn(j_k_ff_4_qn), .preset(and_1_out), .en(and_1_out),
    .reset(and_1_out));  // open: clk
  J_K_Flip_Flop j_k_ff_5 (
    .J(and_11_out), .clk(and_2_out), .K(undriven_4), .Q(j_k_ff_5_q), .en(in_2), .reset(in_2));  // open: Qn, preset
  or or_5 (or_5_out, and_1_out, and_1_out);
  buf and_9 (out_3, in_2);  // AND_Gate
  and and_10 (and_1_out, j_k_ff_4_qn, j_k_ff_3_qn, j_k_ff_1_qn, j_k_ff_1_qn);
  xor xor_5 (and_1_out, j_k_ff_1_qn, out_3);
  buf or_6 (or_6_out, j_k_ff_1_qn);  // OR_Gate
  buf and_11 (and_11_out, j_k_ff_3_qn);  // AND_Gate
endmodule
